// Logisim project ALU_design.circ as structural Verilog: 4 circuits, main circuit ALU_32bits
module ALU_32bits (
  input  [31:0] in_1,
  input  [31:0] in_2,
  input  [3:0] ALU_Op,
  output [31:0] ALU_Result,
  output Zero
);

  wire comparator_1_lt;
  wire [31:0] adder_1_out, extensor_1_32_bits_1_out_2, subtractor_1_out, y_1_out_3;

  Adder #(.width(32)) adder_1 (.a(in_1), .b(in_2), .out(adder_1_out));  // open: cin, cout
  Subtractor #(.width(32)) subtractor_1 (.a(in_1), .b(in_2), .out(subtractor_1_out));  // open: bin, bout
  Comparator #(.width(32)) comparator_1 (.a(in_1), .b(in_2), .lt(comparator_1_lt));  // open: gt, eq
  Y y_1 (.in_1(in_1), .in_2(in_2), .out_3(y_1_out_3));
  Extensor_1_32_bits extensor_1_32_bits_1 (.in_1(comparator_1_lt), .out_2(extensor_1_32_bits_1_out_2));
  Multiplexer #(.select(4), .width(32)) multiplexer_1 (
    .in0(y_1_out_3), .in2(adder_1_out), .in6(subtractor_1_out), .in7(extensor_1_32_bits_1_out_2),
    .out(ALU_Result), .sel(ALU_Op));  // open: in1, in3, in4, in5, in8, in9, in10, in11, in12, in13, in14, in15
  Detector_cero detector_cero_1 (.in_1(ALU_Result), .out_2(Zero));
endmodule

module Y (
  input  [31:0] in_1,
  input  [31:0] in_2,
  output [31:0] out_3
);

  and and_1 (out_3[0], in_1[0], in_2[0]);
  and and_2 (out_3[1], in_1[1], in_2[1]);
  and and_3 (out_3[2], in_1[2], in_2[2]);
  and and_4 (out_3[3], in_1[3], in_2[3]);
  and and_5 (out_3[4], in_1[4], in_2[4]);
  and and_6 (out_3[5], in_1[5], in_2[5]);
  and and_7 (out_3[6], in_1[6], in_2[6]);
  and and_8 (out_3[7], in_1[7], in_2[7]);
  and and_9 (out_3[8], in_1[8], in_2[8]);
  and and_10 (out_3[9], in_1[9], in_2[9]);
  and and_11 (out_3[10], in_1[10], in_2[10]);
  and and_12 (out_3[11], in_1[11], in_2[11]);
  and and_13 (out_3[12], in_1[12], in_2[12]);
  and and_14 (out_3[13], in_1[13], in_2[13]);
  and and_15 (out_3[14], in_1[14], in_2[14]);
  and and_16 (out_3[15], in_1[15], in_2[15]);
  and and_17 (out_3[16], in_1[16], in_2[16]);
  and and_18 (out_3[17], in_1[17], in_2[17]);
  and and_19 (out_3[18], in_1[18], in_2[18]);
  and and_20 (out_3[19], in_1[19], in_2[19]);
  and and_21 (out_3[20], in_1[20], in_2[20]);
  and and_22 (out_3[21], in_1[21], in_2[21]);
  and and_23 (out_3[22], in_1[22], in_2[22]);
  and and_24 (out_3[23], in_1[23], in_2[23]);
  and and_25 (out_3[24], in_1[24], in_2[24]);
  and and_26 (out_3[25], in_1[25], in_2[25]);
  and and_27 (out_3[26], in_1[26], in_2[26]);
  and and_28 (out_3[27], in_1[27], in_2[27]);
  and and_29 (out_3[28], in_1[28], in_2[28]);
  and and_30 (out_3[29], in_1[29], in_2[29]);
  and and_31 (out_3[30], in_1[30], in_2[30]);
  and and_32 (out_3[31], in_1[31], in_2[31]);
endmodule

module Extensor_1_32_bits (
  input  in_1,
  output [31:0] out_2
);


  assign out_2 = {in_1, {31{1'b0}}};
endmodule

module Detector_cero (
  input  [31:0] in_1,
  output out_2
);

  nor nor_1 (out_2, in_1[0], in_1[1], in_1[2], in_1[3], in_1[4], in_1[5], in_1[6], in_1[7], in_1[8], in_1[9], in_1[10], in_1[11], in_1[12], in_1[13], in_1[14], in_1[15], in_1[16], in_1[17], in_1[18], in_1[19], in_1[20], in_1[21], in_1[22], in_1[23], in_1[24], in_1[25], in_1[26], in_1[27], in_1[28], in_1[29], in_1[30], in_1[31]);
endmodule
